# Fritzing sketch HelloRIC_E-PLAN (saved by Fritzing 0.9.5d)
breadboards: 2
perfboards: 3

parts:
  Mod1 = Raspberry Pi 4B
  BAT1 = 12 battery [package=battery]
  J1 = screw terminal, 9 pins
  J2 = screw terminal, 9 pins  # not connected
  J3 = screw terminal, 9 pins
  Fuse1 = Fuse with Handler [part_number=Htc-15m]
  A1 = XY-3606
  J4 = 2.1mm Barrel Jack with Terminal Block
  X1 = USB Connectors [package=usb-a-s-nosilk-female]  # not connected
  X2 = USB Connectors [package=usb-a-s-nosilk-female]  # not connected
  X3 = USB Connectors [package=usb-a-s-nosilk-female]  # not connected
  X4 = USB Connectors [package=usb-a-s-nosilk-female]  # not connected
  JACK1 = 2.1mm DC Barrel Jack  # not connected
  J5 = 2.1mm Barrel Jack with Terminal Block
  USBTTL3 = USB A Plug
  tft1 = 3.5in tft touch screen  # not connected
  J6 = 2.1mm Barrel Jack with Terminal Block
  USBTTL5 = USB A Plug
  USBTTL6 = USB A Plug
  USBTTL7 = USB A Plug
  USBTTL8 = USB A Plug
  X5 = USB Connectors [package=usb-a-s-silk-female]  # not connected
  X6 = USB Connectors [package=usb-a-s-silk-female]  # not connected
  SP1 = SPEAKER [package=pcb_mount_speaker]  # not connected
  USBTTL9 = Micro USB B Plug
  USBTTL10 = USB A Plug
  USBTTL11 = USB A Plug
  J7 = Raspberry Pi Header 40pin [package=THT]
  J8 = female pin header, 2 pins [form="♀ (female)"]  # not connected
  JP1 = Header 3 [package=molex-1x3_lock]  # not connected
  CONN1 = USB connector [package=THT]
  JP2 = USB_MICROB_PLUG [package=micro-b-th]  # not connected
  JP3 = USB_MICROB_PLUG [package=micro-b-th]  # not connected
  JP4 = Header 3 [package=molex-1x3_lock]  # not connected
  J9 = Screw terminal - 2 pins [package=THT]
  J10 = female pin header, 2 pins [form="♀ (female)"]  # not connected
  USBTTL12 = Micro USB B Plug
  USBTTL13 = USB A Plug
  USBTTL14 = Micro USB B Plug
  X7 = USB Connectors [package=usb-a-s-silk-female]  # not connected
  USBTTL15 = Micro USB B Plug
  M1 = RPlidar A1M8 [package=THT]
  CONN2 = USB connector [package=THT]
  USBTTL16 = USB A Plug
  LED1 = DUO LED RG [package="5 mm [THT]"]  # not connected
  LED2 = DUO LED RG [package="5 mm [THT]"]  # not connected
  LED3 = DUO LED RG [package="5 mm [THT]"]  # not connected
  CONN3 = USB connector [package=THT]
  S1 = Pushbutton [package="[THT]"]
  S2 = Pushbutton [package="[THT]"]
  S3 = Pushbutton [package="[THT]"]
  X8 = DB9 Connector [package=db9]  # not connected
  U1 = AVR 10-pin ICSP Header [package="avr icsp"]  # not connected
  J11 = Screw terminal - 2 pins [package=THT]
  J12 = Terminal Block - 2 pins [package=THT]  # not connected
  J13 = Terminal Block - 2 pins [package=THT]  # not connected
  J14 = Terminal Block - 2 pins [package=THT]  # not connected
  USBTTL17 = USB A Plug

nets:
  3V3: Mod1.3V3, J7.3V3
  5V: Mod1.5V, J7.5V
  N1: Mod1.GPIO2, J7.GPIO2
  N2: Mod1.GPIO3, J7.IO3
  GND: Mod1.GND, J7.GND
  N3: Mod1.GPIO4, J7.IO4
  N4: Mod1.GPIO14, J7.IO14
  N5: Mod1.GPIO15, J7.IO15
  N6: Mod1.GPIO17, J7.IO17
  N7: Mod1.GPIO18, J7.IO18
  N8: Mod1.GPIO27, J7.IO22#12
  N9: Mod1.GPIO22, J7.IO22#14
  N10: Mod1.GPIO23, J7.IO23
  N11: Mod1.GPIO24, J7.IO24
  N12: Mod1.GPIO10, J7.IO10
  N13: Mod1.GPIO9, J7.IO9
  N14: Mod1.GPIO25, J7.IO25
  N15: Mod1.GPIO11, J7.IO11
  N16: Mod1.GPIO8, J7.IO8
  N17: Mod1.GPIO7, J7.IO7
  N18: Mod1.ID_SD, J7.IO0
  N19: Mod1.ID_SC, J7.IO1
  N20: Mod1.GPIO5, J7.IO5
  N21: Mod1.GPIO6, J7.IO6
  N22: Mod1.GPIO12, J7.IO12
  N23: Mod1.GPIO13, J7.IO13
  N24: Mod1.GPIO19, J7.IO19
  N25: Mod1.GPIO16, J7.IO16
  N26: Mod1.GPIO26, J7.IO26
  N27: Mod1.GPIO20, J7.IO20
  N28: Mod1.GPIO21, J7.IO21
  N29: BAT1.-, J3.pin6, J6.NEG
  N30: BAT1.+, Fuse1.Connector2, J6.POS
  N31: J1.pin3, J11.pin2
  N32: J1.pin4, J11.pin1
  N33: J3.pin4, J9.pin1
  N34: J3.pin5, A1.Pin_2, A1.Pin_3, J4.NEG, J5.NEG
  N35: J3.pin7, A1.Pin_1, J4.POS
  N36: J3.pin8, J9.pin2
  N37: J3.pin9, Fuse1.Connector1
  N38: A1.Pin_4, J5.POS
  N39: USBTTL3.usb, USBTTL17.usb
  N40: USBTTL5.usb, USBTTL9.usb
  N41: USBTTL6.usb, USBTTL11.usb
  N42: USBTTL7.usb, USBTTL10.usb
  N43: USBTTL8.usb, USBTTL16.usb
  N44: CONN1.GND, CONN1.chassis5, CONN1.chassis6
  N45: USBTTL12.usb, USBTTL13.usb
  N46: USBTTL14.usb, USBTTL15.usb
  N47: M1.pin1, CONN2.d+
  N48: M1.pin2, CONN2.d-
  N49: M1.pin3, CONN2.GND, CONN2.chassis5, CONN2.chassis6
  N50: M1.pin4, CONN2.5V
  N51: CONN3.GND, CONN3.chassis5, CONN3.chassis6
  N52: S1.Pin_1, S1.Pin_2
  N53: S1.Pin_3, S1.Pin_4
  N54: S2.Pin_1, S2.Pin_2
  N55: S2.Pin_3, S2.Pin_4
  N56: S3.Pin_1, S3.Pin_2
  N57: S3.Pin_3, S3.Pin_4

notes:
  12V Batterie
  Terminal
  5A Sicherung
  DC/DC Stepdown Converter
  Input 12V
  Output 5V
  USB 3.0 HUB
  Batterie Stecker
  Speaker Cable
  Monitor Cable
  Touch Cable
  Raspberry PI
  StromPI 2
  (Eigentlich über Raspberry PI)
  12V Input
  Strompi
  Power/Data
  StromPI <--> Raspberry
  HDMI
  LIDAR Sensor
  Touch Display
  Bluetooth Speaker
  Kobuki
  Base I/O
  Status / LED 1 / LED 2
  B0 / B1 / B2
  19V 5A 12V 5A
  12V 5A 5V 1A
  12V Kobuki
  Data
  Raspberry <--> Kobuki
  Serial Port
  Kobuki Power
  LIDAR

custom parts:
  12 battery: 12V lead acid type battery, like the Husqvarna YTH2448 12V 35AH battery. This is the mini version 1/4 the size of the actual battery to be closer to typical breadboard parts (around 2in wide rathher than 7in). The pads in pcb are sized to accomidate up to 14ga wire (as these batterys will deliver high currents.)
  XY-3606: 24V/12V turn 5V 5A power module, DC-DC XY-3606 Power Converter Super LM2596S.
  2.1mm DC Barrel Jack: 2.1mm DC Barrel Jack with Thru-Hole Connectors (breadboardable)
  3.5in tft touch screen: 3.2" tft touch screen lcd display
  Raspberry Pi Header 40pin: Raspberry Pi 40 pin header - for creating your own shields. (Mar 2020, bb: make breadboard friendly (.4in pin spacing) and add labels. Schematic add labels. PCB make oblong pins to allow routing traces between the pins.)
  RPlidar A1M8: .The RPLIDAR A1 is the next generation low cost 360 degree 2D laser scanner (LIDAR) solution developed by SLAMTEC. It can take up to 4000 samples of laser ranging per second with high rotation speed. And equipped with SLAMTEC patented OPTMAG technology, it breakouts the life limitation of traditional LIDAR system so as to work stably for a long time.
  Terminal Block - 2 pins: Generic Screw Terminal 9.5mm
